# Fritzing sketch BlackBox (saved by Fritzing 0.9.2b)
breadboards: 1

parts:
  Part2 = Adafruit ADXL335 [part_number="Adafruit #163"]
  Raspberry_Pi_Zero1 = Raspberry Pi Zero
  Part4 = Adafruit GPS FeatherWing [part_number="Adafruit #3133"]
  Part5 = Adafruit PowerBoost 1000C [part_number="Adafruit #2465"]  # not connected
  BATT1 = LiPoly Battery (1300mAh)  # not connected
  Part7 = Arduino Nano (Rev3.0)
  Part3 = Adafruit BMP180
  R1 = Resistor [tolerance=±5% resistance=1.6k package=THT]
  R2 = Resistor [tolerance=±5% resistance=3.3k package=THT]

nets:
  VIN: Part2.VIN, Part4.3V, Part7.3V3, Part3.+3V3
  GND: Part2.GND, Raspberry_Pi_Zero1.GND, Part4.GND, Part7.GND, Part3.GND, R2.Pin_1
  N1: Part2.ZOUT, Part7.A0
  N2: Part2.YOUT, Part7.A1
  N3: Part2.XOUT, Part7.A2
  N4: Raspberry_Pi_Zero1.GIPO15, R1.Pin_1, R2.Pin_0
  N5: Raspberry_Pi_Zero1.GIPO14, Part7.D6
  N6: Part4.GPS_RX, Part7.D1/TX
  N7: Part4.GPS_TX, Part7.D0/RX
  N8: Part7.D7, R1.Pin_0
  N9: Part7.A5, Part3.SCL
  N10: Part7.A4, Part3.SDA

custom parts:
  Adafruit ADXL335: We've updated our favorite triple-axis accelerometer to now have an on-board 3.3V regulator - making it a perfect choice for interfacing with a 5V microcontroller such as the Arduino. This breakout comes with 3 analog outputs for X, Y and Z axis measurements on a 0.75"x0.75" breakout board. The ADXL335 is the latest and greatest from Analog Devices, known for their exceptional quality MEMS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
  Adafruit GPS FeatherWing: Give your Feather a sense of place, with an Ultimate GPS FeatherWing. In 2013 we designed the Ultimate GPS module to satisfy all your GPS desires - and now we have brought its power and versatility plus more to our Feather series with the Adafruit Ultimate GPS FeatherWing! This FeatherWing plugs right into your Feather board and gives it a precise, sensitive, and low power GPS module for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
  Adafruit PowerBoost 1000C: PowerBoost 1000C is the perfect power supply for your portable project! With a built-in load-sharing battery charger circuit, you'll be able to keep your power-hungry project running even while recharging the battery! This little DC/DC boost converter module can be powered by any 3.7V LiIon/LiPoly battery, and convert the battery output to 5.2V DC for running your 5V projects.
  LiPoly Battery (1300mAh): Lithium Ion Polymer Battery (1300mAh)
  Adafruit BMP180: This precision sensor from Bosch is the best low-cost sensing solution for measuring barometric pressure and temperature. Because pressure changes with altitude you can also use it as an altimeter! The sensor is soldered onto a PCB with a 3.3V regulator, I2C level shifter and pull-up resistors on the I2C pins. The BMP180 is the next-generation of sensors from Bosch, and replaces the BMP085.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
